// Digital circuit cicuit.dig as structural Verilog
module cicuit (
  input  in_1
);

  wire not_1_out;
  wire [3:0] add_1_s, register_1_q, u_INST_DECODER_op_code, u_INST_DECODER_out_imm4;
  wire [7:0] u_INST_DECODER_out_imm8;
  wire [15:0] Instruction_Ram_d;

  Register #(.Bits(4)) register_1 (.D(add_1_s), .C(in_1), .en(1'b1), .Q(register_1_q));
  // Probe on register_1_q
  not not_1 (not_1_out, in_1);
  RAMDualPort #(.AddrBits(4), .Bits(16)) Instruction_Ram (
    .A(register_1_q), .Din({16{1'b0}}), .str(1'b0), .C(not_1_out), .ld(1'b1), .D(Instruction_Ram_d));
  Add #(.Bits(4)) add_1 (.a(register_1_q), .b(4'b0001), .c_i(1'b0), .s(add_1_s));  // open: c_o
  // Probe on Instruction_Ram_d
  INST_DECODER #(.applicationType("GHDL"), .CodeFile("D:\\github\\uffs-arquivos\\SEM4\\org\\proc18bits\\instruction_decoder.vhd")) u_INST_DECODER (
    .inst(Instruction_Ram_d), .op_code(u_INST_DECODER_op_code), .out_imm4(u_INST_DECODER_out_imm4),
    .out_imm8(u_INST_DECODER_out_imm8));  // open: out_rs1, out_rs2, out_rd
  CONTROLL #(.applicationType("GHDL"), .CodeFile("D:\\github\\uffs-arquivos\\SEM4\\org\\proc18bits\\controll.vhd")) u_CONTROLL (.inst(u_INST_DECODER_op_code));  // open: reg_write
  RegisterFile registerfile_1 ();  // open: Din, we, Rw, C, Ra, Rb, Da, Db
  IMMGEN #(.applicationType("GHDL"), .CodeFile("D:\\github\\uffs-arquivos\\SEM4\\org\\proc18bits\\imm_gen.vhd")) u_IMMGEN (
    .imm4(u_INST_DECODER_out_imm4), .imm8(u_INST_DECODER_out_imm8));  // open: out_imm4, out_imm8
  RAMDualPort Data_Ram ();  // open: A, Din, str, C, ld, D
endmodule
