// Digital circuit processador8Bits.dig as structural Verilog
module processador8Bits (
  input  [7:0] dado_a_ser_armazenado,
  input  \_1___dado_é_armazenado ,
  input  [2:0] seleciona_registrador,
  input  in_4,
  input  [2:0] in_5,
  input  [2:0] in_6,
  input  [3:0] \endereço_onde_pegar___armazenar ,
  input  [7:0] dado_a_ser_armazenado_2,
  input  _1___dado_armazenado_no_clock,
  input  in_13,
  input  in_14,
  input  in_15,
  output [7:0] out_7,
  output [7:0] out_8,
  output [7:0] out_9,
  output Terminado
);

  wire u_BR_CONTROLLER_id, u_BR_CONTROLLER_str, u_BR_CONTROLLER_value_in_select, u_BR_CONTROLLER_we,
       u_INSTRUCTION_MEMORY_valid_clk;
  wire [2:0] u_BR_CONTROLLER_a, u_BR_CONTROLLER_ra, u_BR_CONTROLLER_rb, u_BR_CONTROLLER_rw,
       u_INST_DECODER_inst_code, u_INST_DECODER_reg_a, u_INST_DECODER_reg_b, u_INST_DECODER_reg_dest;
  wire [7:0] multiplexer_1_out, ramdualport_1_d, registerfile_1_da, registerfile_1_db, u_BR_CONTROLLER_din,
       u_BR_CONTROLLER_ram, u_BR_CONTROLLER_ula_a, u_BR_CONTROLLER_ula_b, u_INST_DECODER_cnst, u_ULA_s;
  wire [11:0] u_INSTRUCTION_MEMORY_instruction;

  INSTRUCTION_MEMORY #(.applicationType("GHDL"), .CodeFile("D:\\github\\uffs-arquivos\\SEM4\\org\\processador8bits\\instruction_memory.vhd")) u_INSTRUCTION_MEMORY (
    .clk(in_15), .instruction(u_INSTRUCTION_MEMORY_instruction), .valid_clk(u_INSTRUCTION_MEMORY_valid_clk));
  INST_DECODER #(.applicationType("GHDL"), .CodeFile("D:\\github\\uffs-arquivos\\SEM4\\org\\processador8bits\\inst_decoder.vhd")) u_INST_DECODER (
    .operation(u_INSTRUCTION_MEMORY_instruction), .reg_dest(u_INST_DECODER_reg_dest),
    .reg_a(u_INST_DECODER_reg_a), .reg_b(u_INST_DECODER_reg_b), .inst_code(u_INST_DECODER_inst_code),
    .cnst(u_INST_DECODER_cnst));
  RegisterFile #(.AddrBits(3), .Bits(8)) BANCO (
    .Din(dado_a_ser_armazenado), .we(\_1___dado_é_armazenado ), .Rw(seleciona_registrador), .C(in_4),
    .Ra(in_5), .Rb(in_6), .Da(out_7), .Db(out_8));
  Multiplexer #(.Bits(8)) multiplexer_1 (
    .sel(u_BR_CONTROLLER_value_in_select), .in_0(u_ULA_s), .in_1(ramdualport_1_d), .out(multiplexer_1_out));
  BR_CONTROLLER #(.applicationType("GHDL"), .CodeFile("D:\\github\\uffs-arquivos\\SEM4\\org\\processador8bits\\br_controller.vhd")) u_BR_CONTROLLER (
    .da(registerfile_1_da), .db(registerfile_1_db), .reg_dest(u_INST_DECODER_reg_dest),
    .reg_a(u_INST_DECODER_reg_a), .reg_b(u_INST_DECODER_reg_b), .inst(u_INST_DECODER_inst_code),
    .cnst(u_INST_DECODER_cnst), .value_in(multiplexer_1_out), .valid_clk(u_INSTRUCTION_MEMORY_valid_clk),
    .din(u_BR_CONTROLLER_din), .we(u_BR_CONTROLLER_we), .rw(u_BR_CONTROLLER_rw), .ra(u_BR_CONTROLLER_ra),
    .rb(u_BR_CONTROLLER_rb), .a(u_BR_CONTROLLER_a), .ram(u_BR_CONTROLLER_ram), .str(u_BR_CONTROLLER_str),
    .id(u_BR_CONTROLLER_id), .ula_a(u_BR_CONTROLLER_ula_a), .ula_b(u_BR_CONTROLLER_ula_b),
    .value_in_select(u_BR_CONTROLLER_value_in_select), .end_process(Terminado));
  RegisterFile #(.AddrBits(3), .Bits(8)) registerfile_1 (
    .Din(u_BR_CONTROLLER_din), .we(u_BR_CONTROLLER_we), .Rw(u_BR_CONTROLLER_rw), .C(in_15),
    .Ra(u_BR_CONTROLLER_ra), .Rb(u_BR_CONTROLLER_rb), .Da(registerfile_1_da), .Db(registerfile_1_db));
  // Probe on multiplexer_1_out
  RAMDualPort #(.AddrBits(3), .isProgramMemory("true"), .Bits(8)) ramdualport_1 (
    .A(u_BR_CONTROLLER_a), .Din(u_BR_CONTROLLER_ram), .str(u_BR_CONTROLLER_str), .C(in_15),
    .ld(u_BR_CONTROLLER_id), .D(ramdualport_1_d));
  // Probe on u_BR_CONTROLLER_din
  // Probe on u_BR_CONTROLLER_ula_a
  // Probe on u_BR_CONTROLLER_ula_b
  ULA #(.applicationType("GHDL"), .CodeFile("D:\\github\\uffs-arquivos\\SEM4\\org\\processador8bits\\ula.vhd")) u_ULA (
    .a(u_BR_CONTROLLER_ula_a), .b(u_BR_CONTROLLER_ula_b), .op(u_INST_DECODER_inst_code), .s(u_ULA_s));
  // Probe on u_INST_DECODER_inst_code
  // Probe on u_ULA_s
  RAMDualPort #(.AddrBits(4), .Bits(8)) ramdualport_2 (
    .A(\endereço_onde_pegar___armazenar ), .Din(dado_a_ser_armazenado_2),
    .str(_1___dado_armazenado_no_clock), .C(in_13), .ld(in_14), .D(out_9));

  // Notes on the sheet:
  //   Terminado: Terminado
endmodule
