// Digital circuit testes.dig as structural Verilog
module testes (
  input  [3:0] in_1,
  input  [7:0] in_6,
  input  [7:0] in_7,
  input  [2:0] in_8,
  input  [7:0] dado_a_ser_armazenado,
  input  \_1___dado_é_armazenado ,
  input  [2:0] seleciona_registrador,
  input  in_14,
  input  [2:0] in_15,
  input  [2:0] in_16,
  input  [3:0] \endereço_onde_pegar___armazenar ,
  input  [7:0] dado_a_ser_armazenado_2,
  input  _1___dado_armazenado_no_clock,
  input  in_23,
  input  in_24,
  output [2:0] out_2,
  output [2:0] out_3,
  output [2:0] out_4,
  output [2:0] out_5,
  output [7:0] out_9,
  output [7:0] out_10,
  output [7:0] out_17,
  output [7:0] out_18,
  output [7:0] out_19
);

  wire [11:0] u_INSTRUCTION_MEMORY_instruction;

  RegisterFile #(.AddrBits(3), .Bits(8)) BANCO (
    .Din(dado_a_ser_armazenado), .we(\_1___dado_é_armazenado ), .Rw(seleciona_registrador), .C(in_14),
    .Ra(in_15), .Rb(in_16), .Da(out_17), .Db(out_18));
  ULA #(.applicationType("GHDL"), .CodeFile("D:\\github\\uffs-arquivos\\SEM4\\org\\processador8bits\\ula.vhd")) u_ULA (
    .a(in_6), .b(in_7), .op(in_8), .s(out_9));
  INSTRUCTION_MEMORY #(.applicationType("GHDL"), .CodeFile("D:\\github\\uffs-arquivos\\SEM4\\org\\processador8bits\\instruction_memory.vhd")) u_INSTRUCTION_MEMORY (
    .pc(in_1), .instruction(u_INSTRUCTION_MEMORY_instruction));
  INST_DECODER #(.applicationType("GHDL"), .CodeFile("D:\\github\\uffs-arquivos\\SEM4\\org\\processador8bits\\inst_decoder.vhd")) u_INST_DECODER (
    .operation(u_INSTRUCTION_MEMORY_instruction), .reg_dest(out_2), .reg_a(out_3), .reg_b(out_4),
    .inst_code(out_5), .cnst(out_10));
  RAMDualPort #(.AddrBits(4), .isProgramMemory("true"), .Bits(8)) ramdualport_1 (
    .A(\endereço_onde_pegar___armazenar ), .Din(dado_a_ser_armazenado_2),
    .str(_1___dado_armazenado_no_clock), .C(in_23), .ld(in_24), .D(out_19));
endmodule
